# Fritzing sketch MAINPOWER (saved by Fritzing 0.9.3b)
circuit board: 19.74cm x 13.41cm

parts:
  LED1 = MOSFET-NCHANNEL [package=to220v]
  R1 = Resistor [tolerance=±5% resistance=330 package=THT]
  R2 = Resistor [tolerance=±5% resistance=1k package=THT]
  LED2 = MOSFET-NCHANNEL [package=to220v]
  R3 = Resistor [tolerance=±5% resistance=330 package=THT]
  R4 = Resistor [tolerance=±5% resistance=1k package=THT]
  LED3 = MOSFET-NCHANNEL [package=to220v]
  R5 = Resistor [tolerance=±5% resistance=330 package=THT]
  R6 = Resistor [tolerance=±5% resistance=1k package=THT]
  LED4 = MOSFET-NCHANNEL [package=to220v]
  R7 = Resistor [tolerance=±5% resistance=330 package=THT]
  R8 = Resistor [tolerance=±5% resistance=1k package=THT]
  IC2 = Voltage Regulator [package=to220-igo]
  R9 = Resistor [tolerance=±5% resistance=1k package=THT]
  C2 = Tantalum Capacitor [capacitance=0.1µF package="100 mil [THT, tantalum]"]
  Photodiode_Out/In1 = Generic shrouded header - 6 pins [form="♂ (shrouded male)" package=THT]
  DB9_OUT = shrouded pin header, 10 pins [form="♂ (shrouded male)"]
  12V_POWER_IN = screw terminal, 2 pins
  LED5 = MOSFET-NCHANNEL [package=to220v]
  R12 = Resistor [tolerance=±5% resistance=330 package=THT]
  R13 = Resistor [tolerance=±5% resistance=1k package=THT]
  J1 = Generic shrouded header - 6 pins [form="♂ (shrouded male)" package=THT]
  Arduino_UNO1 = Arduino Uno (Rev3) - ICSP
  Motor_Y = Header 4 [package=jst-4-pth]
  Motor_X = Header 4 [package=jst-4-pth]
  J2 = male pin header, 4 pins [form="♂ (male)"]
  J3 = male pin header, 4 pins [form="♂ (male)"]

nets:
  N1: LED1.G, R1.Pin_1
  N2: LED1.D, J1.GND
  GND: LED1.S, R2.Pin_1, LED2.S, R4.Pin_1, LED3.S, R6.Pin_1, LED4.S, R8.Pin_1, IC2.GND, C2.-, Photodiode_Out/In1.GND, DB9_OUT.pin9, 12V_POWER_IN.pin1, LED5.S, R13.Pin_1, Arduino_UNO1.GND, Motor_Y.2, Motor_X.2, J2.pin1
  N3: R1.Pin_0, R2.Pin_0, Arduino_UNO1.D8
  N4: LED2.G, R3.Pin_1
  N5: LED2.D, J1.D6
  N6: R3.Pin_0, R4.Pin_0, Arduino_UNO1.D7
  N7: LED3.G, R5.Pin_1
  N8: LED3.D, J1.LED_(+)
  N9: R5.Pin_0, R6.Pin_0, Arduino_UNO1.D4
  N10: LED4.G, R7.Pin_1
  N11: LED4.D, J1.LED_(-)
  N12: R7.Pin_0, R8.Pin_0, Arduino_UNO1.D2
  N13: IC2.IN, DB9_OUT.pin2, 12V_POWER_IN.pin2, J1.5V, Motor_Y.1, Motor_X.1
  N14: IC2.OUT, R9.Pin_1, DB9_OUT.pin1
  N15: R9.Pin_0, C2.+, Photodiode_Out/In1.5V
  N16: Photodiode_Out/In1.SIGNAL, Arduino_UNO1.A0, J3.pin4
  N17: DB9_OUT.pin3, Arduino_UNO1.A1
  N18: DB9_OUT.pin4, Arduino_UNO1.A2
  N19: DB9_OUT.pin5, Arduino_UNO1.A3
  N20: DB9_OUT.pin7, Arduino_UNO1.ICSP_MISO, Arduino_UNO1.D12/MISO
  N21: DB9_OUT.pin8, Arduino_UNO1.D10_PWM/SS
  N22: DB9_OUT.pin10, Arduino_UNO1.ICSP_MOSI, Arduino_UNO1.D11_PWM/MOSI
  N23: LED5.G, R12.Pin_1
  N24: LED5.D, J1.pin6
  N25: R12.Pin_0, R13.Pin_0, Arduino_UNO1.D6_PWM
  N26: Arduino_UNO1.A5/SCL, Motor_Y.4
  N27: Arduino_UNO1.D9_PWM, Motor_X.3
  N28: Arduino_UNO1.A4/SDA, Motor_X.4
  N29: Arduino_UNO1.D5_PWM, Motor_Y.3
  N30: J2.pin4, J3.pin1

notes:
  12V (+)
  GND
  G
  D
  S
  IN
  OUT
  12V
  1k
  330
  .1uF
  Photodiode Resistors
  In
  Out
  Photodiode Connector
  LED Connector
  Auxiliary Connector

custom parts:
  Generic shrouded header - 6 pins: Generic shrouded header
  Generic shrouded header - 6 pins: Generic shrouded header
