# Fritzing sketch POWERSWITCH_BOARD (saved by Fritzing 0.9.3b)
circuit board: 4.70285cm x 4.629cm

parts:
  S1 = SWITCH-SPST-2 [package=switch-spst-vertical]
  J1 = Screw terminal - 2 pins [package=THT]

nets:
  N1: S1.O, J1.pin2
  N2: S1.P, J1.pin1

notes:
  12V (IN)
  12V (OUT)
