# Fritzing sketch LED_CIRCUIT (saved by Fritzing 0.9.3b)
circuit board: 7.68cm x 4.69cm
breadboards: 1

parts:
  LED_2 = Header 2 [package=jst-2-pth]
  LED_3 = Header 2 [package=jst-2-pth]
  LED_1 = Header 2 [package=jst-2-pth]
  Power_In = Generic shrouded header - 6 pins [form="♂ (shrouded male)" package=THT]
  LED_4 = Header 2 [package=jst-2-pth]
  LED_5 = Header 2 [package=jst-2-pth]
  LED_6 = Header 2 [package=jst-2-pth]
  J6 = female pin header, 4 pins [form="♀ (female)"]
  J5 = female pin header, 4 pins [form="♀ (female)"]
  J4 = female pin header, 4 pins [form="♀ (female)"]
  J3 = female pin header, 4 pins [form="♀ (female)"]
  J1 = female pin header, 4 pins [form="♀ (female)"]
  J2 = female pin header, 4 pins [form="♀ (female)"]

nets:
  N1: LED_2.1, J1.pin4
  N2: LED_2.2, Power_In.LED2_(-)
  N3: LED_3.1, J3.pin4
  N4: LED_3.2, Power_In.LED3_(-)
  N5: LED_1.1, J2.pin4
  N6: LED_1.2, Power_In.LED1_(-)
  N7: Power_In.LED_(+), J6.pin1, J5.pin1, J4.pin1, J3.pin1, J1.pin1, J2.pin1
  N8: Power_In.pin_5, LED_4.2
  N9: Power_In.pin6, LED_5.2, LED_6.2
  N10: LED_4.1, J4.pin4
  N11: LED_5.1, J5.pin4
  N12: LED_6.1, J6.pin4

notes:
  +
  -

custom parts:
  Generic shrouded header - 6 pins: Generic shrouded header
