# Fritzing sketch PHOTODIODE_CIRCUIT (saved by Fritzing 0.9.3b)
circuit board: 3.99999cm x 3.99999cm
breadboards: 1

parts:
  J1 = Generic shrouded header - 6 pins [form="♂ (shrouded male)" package=THT]
  P1 = FDS100 - Final [package="8mm Ceramic [THT]"]

nets:
  N1: J1.LED_(+), P1.pin_3
  N2: J1.LED1_(-), P1.pin_2
  N3: J1.LED2_(-), P1.pin_1

notes:
  3
  2
  1

custom parts:
  Generic shrouded header - 6 pins: Generic shrouded header
  FDS100 - Final: S1133 photodiode with low dark current by Hamamatsu.
